# Fritzing sketch bldc1 (saved by Fritzing 0.9.3b)
circuit board: 8.46667cm x 5.64444cm
breadboards: 1

parts:
  R1 = Resistor [tolerance=±5% resistance=220 package=THT]
  LED1 = LED - 5mm [color="Red (633nm)" package="5 mm [THT]"]
  R2 = Resistor [tolerance=±5% resistance=220 package=THT]
  LED2 = LED - 5mm [color="Red (633nm)" package="5 mm [THT]"]
  R3 = Resistor [tolerance=±5% resistance=220 package=THT]
  LED3 = LED - 5mm [color="Red (633nm)" package="5 mm [THT]"]
  ds1809 = IC, DIP package, 8 pins [chip_label=DS1809]
  HallPwr = DC Power [voltage=6.25]
  Part1 = Arduino Prototyping Shield
  Q1 = npn-Powertransistor [package="TO220 [THT]"]  # not connected
  Rocker = Trimmer Potentiometer [maximum_resistance=10kΩ package=THT]

nets:
  N1: R1.Pin_0, LED1.anode
  N2: R1.Pin_1, R2.Pin_1, R3.Pin_1, ds1809.pin8, Part1.+5V, Rocker.leg2
  HallA: LED1.cathode, LED3.cathode, Part1.D2, Part1.D4
  N3: R2.Pin_0, LED2.anode
  HallC: LED2.cathode, Part1.D3
  N4: R3.Pin_0, LED3.anode
  N5: ds1809.pin1, HallPwr.V+
  N6: ds1809.pin2, Part1.D6
  N7: ds1809.pin3, ds1809.pin4, HallPwr.V-
  N8: ds1809.pin5, Part1.GND
  PotWpr: ds1809.pin6
  N9: ds1809.pin7, Part1.D5
  N10: Part1.A0, Rocker.wiper
  GND: Rocker.leg1
